// Logisim project decoder_2to4 (1).circ as structural Verilog: 1 circuit, main circuit decoder_2to4
module decoder_2to4 (
  input  A,
  input  B,
  output D0,
  output D1,
  output D2,
  output D3
);

  wire not_1_out, not_2_out, undriven, undriven_2, undriven_3, undriven_4, undriven_5, undriven_6;

  not not_1 (not_1_out, A);
  not not_2 (not_2_out, B);
  and and_1 (D0, not_1_out, not_2_out);
  and and_2 (D1, undriven_3, undriven_4);
  and and_3 (D2, undriven, undriven_6);
  and and_4 (D3, undriven_2, undriven_5);
endmodule
