// Logisim project decoder_3to8_large.circ as structural Verilog: 1 circuit, main circuit decoder_3to8
module decoder_3to8 (
  input  A,
  input  B,
  input  C,
  output D0,
  output D1,
  output D2,
  output D3,
  output D4,
  output D5,
  output D6,
  output D7
);

  wire not_1_out, not_2_out, not_3_out, undriven, undriven_2, undriven_3, undriven_4, undriven_5, undriven_6,
       undriven_7, undriven_8, undriven_9, undriven_10, undriven_11, undriven_12, undriven_13, undriven_14,
       undriven_15, undriven_16, undriven_17, undriven_18, undriven_19, undriven_20, undriven_21;

  not not_1 (not_1_out, A);
  not not_2 (not_2_out, B);
  not not_3 (not_3_out, C);
  and and_1 (D0, not_1_out, not_2_out, not_3_out);
  and and_2 (D1, undriven_5, undriven_12, undriven_15);
  and and_3 (D2, undriven_6, undriven_8, undriven_19);
  and and_4 (D3, undriven_7, undriven_9, undriven_16);
  and and_5 (D4, undriven, undriven_13, undriven_20);
  and and_6 (D5, undriven_2, undriven_14, undriven_17);
  and and_7 (D6, undriven_3, undriven_10, undriven_21);
  and and_8 (D7, undriven_4, undriven_11, undriven_18);
endmodule
