// Logisim project timers_and_splitters_PERFECT (2).circ as structural Verilog: 1 circuit, main circuit main
module main (
  input  Bit_0__LSB,
  input  Bit_1,
  input  [3:0] Bus_In__3_0,
  input  Bit_2,
  input  Bit_3__MSB,
  input  [3:0] Timer_Count__3_0
);

  wire [3:0] Clock_Source__1_Hz_out;

  Clock #(.highDuration(500), .lowDuration(500)) Clock_Source__1_Hz (.out(Clock_Source__1_Hz_out[0]));
  Counter #(.width(4), .max('hf)) _4_BIT_TIMER___COUNTER (
    .D(Clock_Source__1_Hz_out), .Q(Clock_Source__1_Hz_out));  // open: load, count, carry, clk, clr
  // Pins of 1 and 4 bits meet at Clock_Source__1_Hz_out

  assign {Bus_In__3_0[3], Bus_In__3_0[1:0]} = {Bit_3__MSB, Bit_1, Bit_0__LSB};

  // Notes on the sheet:
  //   1. BIT SPLITTER — 4-Bit Vector Demultiplexing
  //   Splits one 4-bit parallel bus into four independent 1-bit signals
  //   2. CLOCK-DRIVEN TIMER — 4-Bit Sequential Counter
  //   Counts 0000 → 0001 → 0010 → ... → 1111 → 0000 on rising clock edges
  //   Example: 1 Hz clock = one count per second; 0–15 s cycle
endmodule
